// Logisim project Practica05.circ as structural Verilog
module automata (
  input  In
);

  wire clock_1_out, E1_qn, E2_qn, not_1_out, R1_out, S1_out, S2_out;
  wire [1:0] E2_q;

  Clock clock_1 (.out(clock_1_out));
  not not_1 (not_1_out, In);
  S_R_Flip_Flop E1 (.S(S1_out), .clk(clock_1_out), .R(R1_out), .Q(E2_q[1]), .Qn(E1_qn));  // open: preset, reset, en
  S_R_Flip_Flop E2 (.S(S2_out), .clk(clock_1_out), .R(E2_q[0]), .Q(E2_q[0]), .Qn(E2_qn));  // open: preset, reset, en
  and S1 (S1_out, E1_qn, E2_q[0], not_1_out);
  and R1 (R1_out, E2_q[1], E2_q[0], not_1_out);
  and S2 (S2_out, E2_qn, not_1_out);
  Hex_Digit_Display hex_digit_display_1 (.value({2'b00, E2_q}));  // open: dp

  // Notes on the sheet:
  //   Entrada del autómata
  //   0 = error
  //   1 = acierto
  //   Autómata del ejercicio 1
  //   R2
  //   Estado actual del autómata.
  //   0 = T
  //   1 = TE
  //   2 = NT
  //   3 = NTE
endmodule

module registro (
  input  Leer,
  input  Escribir,
  input  [7:0] Dato_a_escribir,
  output [7:0] \Dato_leído 
);

  wire Reloj_out;
  wire [7:0] d_ff_1_q, multiplexer_1_out;

  Clock Reloj (.out(Reloj_out));
  Multiplexer #(.width(8), .enable("false")) multiplexer_1 (
    .in0(d_ff_1_q), .in1(Dato_a_escribir), .out(multiplexer_1_out), .sel(Escribir));
  D_Flip_Flop d_ff_1 (.clk(Reloj_out), .D(multiplexer_1_out[0]), .Q(d_ff_1_q[0]));  // open: Qn, preset, en, reset
  D_Flip_Flop d_ff_2 (.clk(Reloj_out), .D(multiplexer_1_out[1]), .Q(d_ff_1_q[1]));  // open: Qn, preset, en, reset
  D_Flip_Flop d_ff_3 (.clk(Reloj_out), .D(multiplexer_1_out[2]), .Q(d_ff_1_q[2]));  // open: Qn, preset, en, reset
  D_Flip_Flop d_ff_4 (.clk(Reloj_out), .D(multiplexer_1_out[3]), .Q(d_ff_1_q[3]));  // open: Qn, preset, en, reset
  D_Flip_Flop d_ff_5 (.clk(Reloj_out), .D(multiplexer_1_out[4]), .Q(d_ff_1_q[4]));  // open: Qn, preset, en, reset
  D_Flip_Flop d_ff_6 (.clk(Reloj_out), .D(multiplexer_1_out[5]), .Q(d_ff_1_q[5]));  // open: Qn, preset, en, reset
  D_Flip_Flop d_ff_7 (.clk(Reloj_out), .D(multiplexer_1_out[6]), .Q(d_ff_1_q[6]));  // open: Qn, preset, en, reset
  D_Flip_Flop d_ff_8 (.clk(Reloj_out), .D(multiplexer_1_out[7]), .Q(d_ff_1_q[7]));  // open: Qn, preset, en, reset
  Multiplexer #(.width(8), .enable("false")) multiplexer_2 (
    .in0({8{1'b0}}), .in1(d_ff_1_q), .out(\Dato_leído ), .sel(Leer));

  // Notes on the sheet:
  //   Registro de 8 bits usando flip-flop's D
endmodule

module XOR (
  input  [7:0] P,
  input  [7:0] Q,
  output [7:0] P_XOR_Q
);

  wire [7:0] and_1_out, and_2_out, not_1_out, not_2_out;

  assign not_1_out = ~P;  // NOT_Gate not_1, 8 bits wide
  assign not_2_out = ~Q;  // NOT_Gate not_2, 8 bits wide
  assign and_1_out = not_1_out & Q;  // AND_Gate and_1, 8 bits wide
  assign and_2_out = P & not_2_out;  // AND_Gate and_2, 8 bits wide
  assign P_XOR_Q = and_1_out | and_2_out;  // OR_Gate or_1, 8 bits wide

  // Notes on the sheet:
  //   Compuerta XOR de 8 bits
endmodule
